// Logisim project SD_Group07.circ as structural Verilog: 4 circuits, main circuit main
module main (
  output [11:0] pc,
  output [11:0] r0,
  output [11:0] r1,
  output [11:0] r2,
  output [11:0] r3,
  output [11:0] r4,
  output [11:0] r5,
  output [11:0] r6,
  output [11:0] r7,
  output halt
);

  wire and_1_out, clock_1_out, reset_out, undriven, undriven_2, undriven_3, undriven_4;
  wire [11:0] multiplexer_1_out, n12_bit_alu_2_result, program_counter_1_out_6, ram_2_data,
       register_file_1_s, register_file_1_t, register_file_2_s, register_file_2_t;
  wire [12:0] ram_1_data;

  Halt halt_1 (.instruction(ram_1_data), .clock(clock_1_out), .reset(reset_out), .halt(halt));
  Clock clock_1 (.out(clock_1_out));
  Button reset (.out(reset_out));
  and and_1 (and_1_out, ~halt, clock_1_out);  // AND_Gate
  program_counter program_counter_1 (
    .Branch_relative(1'b0), .Branch_absolute(1'b0), .C(and_1_out), .Reset(1'b0),
    .out_6(program_counter_1_out_6));  // open: Branch_value
  register_file register_file_1 (
    .S(register_file_1_s), .T(register_file_1_t));  // open: rs, rt, rd, data, write, clock, reset
  RAM #(.addrWidth(12), .dataWidth(13)) ram_1 (
    .addr(program_counter_1_out_6), .data(ram_1_data), .clk(and_1_out));  // open: sel, ld, clr
  _12_bit_ALU u_12_bit_alu_1 (.a(register_file_1_s), .b(register_file_1_t));  // open: ALU_code, overflow, result
  register_file register_file_2 (
    .rs(ram_1_data[9:7]), .rt(ram_1_data[12:10]), .rd(ram_1_data[6:4]), .data(multiplexer_1_out),
    .write(undriven), .clock(and_1_out), .reset(1'b0), .S(register_file_2_s), .T(register_file_2_t));
  _12_bit_ALU u_12_bit_alu_2 (
    .a(register_file_2_s), .b(register_file_2_t), .result(n12_bit_alu_2_result));  // open: ALU_code, overflow
  RAM #(.addrWidth(12), .dataWidth(12), .bus("separate")) ram_2 (
    .addr(n12_bit_alu_2_result), .din(register_file_2_t), .data(ram_2_data), .str(undriven_2),
    .clk(and_1_out), .ld(undriven_3));  // open: sel, clr
  Multiplexer #(.width(12), .enable("false")) multiplexer_1 (
    .in0(ram_2_data), .in1(n12_bit_alu_2_result), .out(multiplexer_1_out), .sel(undriven_4));

  // Notes on the sheet:
  //   current instruction
  //   clock signal
  //   reset button
  //   RegWrite
  //   DO NOT CHANGE THE INPUTS AND OUTPUTS OF THIS CIRCUIT! Do not add/remove inputs or outputs. Do not even change their location or orientation.
  //   MemToReg
  //   Memwrite
  //   Memread
endmodule

module Halt (
  input  [12:0] instruction,
  input  clock,
  input  reset,
  output halt
);

  wire and_1_out, comparator_1_eq, comparator_2_gt, counter_1_carry, or_1_out, or_2_out;
  wire [11:0] counter_1_q;

  Comparator #(.width(13), .mode("unsigned")) comparator_1 (
    .a(instruction), .b({13{1'b0}}), .eq(comparator_1_eq));  // open: gt, lt
  Counter #(.width(12), .max('hfff), .trigger("falling")) counter_1 (
    .Q(counter_1_q), .carry(counter_1_carry), .clk(clock), .clr(reset));  // open: load, D, count
  or or_1 (or_1_out, comparator_1_eq, counter_1_carry);
  Comparator #(.width(12), .mode("unsigned")) comparator_2 (
    .a(counter_1_q), .b({12{1'b0}}), .gt(comparator_2_gt));  // open: eq, lt
  or or_2 (or_2_out, halt, and_1_out);
  and and_1 (and_1_out, or_1_out, comparator_2_gt);
  Register #(.width(1)) register_1 (.D(or_2_out), .Q(halt), .clk(clock), .clr(reset));  // open: en

  // Notes on the sheet:
  //   halt becomes and stays asserted if the instruction is 0000 (not in the first clock cycle) or the end of the counter is reached (2^12)
endmodule

module program_counter (
  input  Branch_relative,
  input  Branch_absolute,
  input  [11:0] Branch_value,
  input  C,
  input  Reset,
  output [11:0] out_6
);

  wire and_1_out;
  wire [1:0] priority_encoder_1_out;
  wire [11:0] multiplexer_1_out, n12bit_cla_1_out_4, n12bit_cla_2_out_4;

  _12bit_CLA u_12bit_cla_1 (
    .in_1(Branch_value), .in_2(out_6), .in_3(1'b0), .out_4(n12bit_cla_1_out_4));  // open: Overflow
  and and_1 (and_1_out, ~Branch_relative, ~Branch_absolute);  // AND_Gate
  Priority_Encoder #(.select(2)) priority_encoder_1 (
    .in0(Branch_relative), .in1(Branch_absolute), .in2(and_1_out), .out(priority_encoder_1_out));  // open: in3, gs, en_out, en_in
  Multiplexer #(.select(2), .width(12), .enable("false")) multiplexer_1 (
    .in0(n12bit_cla_1_out_4), .in1(Branch_value), .in2(n12bit_cla_2_out_4), .out(multiplexer_1_out),
    .sel(priority_encoder_1_out));  // open: in3
  _12bit_register u_12bit_register_1 (.Input(multiplexer_1_out), .Reset(Reset), .Write(1'b1), .Clock(C), .out_5(out_6));
  _12bit_CLA u_12bit_cla_2 (.in_1(out_6), .in_2(12'h1), .in_3(1'b0), .out_4(n12bit_cla_2_out_4));  // open: Overflow
endmodule

module Control_Logic (
  input  [12:0] in_1,
  output RegWrite,
  output MemToReg,
  output MemWrite,
  output MemRead,
  output [3:0] ALU
);

  wire and_1_out, and_2_out, not_1_out, not_2_out, not_3_out, not_4_out, not_6_out, not_7_out, not_8_out,
       or_1_out;
  wire [3:0] bit_extender_1_out, multiplexer_1_out;

  assign bit_extender_1_out = {{1{1'b1}}, in_1[12:10]};  // Bit_Extender bit_extender_1
  not not_1 (not_1_out, in_1[0]);
  not not_2 (not_2_out, in_1[1]);
  not not_3 (not_3_out, in_1[2]);
  not not_4 (not_4_out, in_1[3]);
  and and_1 (and_1_out, not_1_out, not_2_out, not_3_out, not_4_out);
  and and_2 (and_2_out, ~and_1_out, ~MemRead, ~MemWrite);  // AND_Gate
  Multiplexer #(.width(4), .enable("false")) multiplexer_1 (
    .in0(in_1[3:0]), .in1(bit_extender_1_out), .out(multiplexer_1_out), .sel(and_2_out));
  and and_3 (MemRead, in_1[0], not_2_out, not_3_out, in_1[3]);
  and and_4 (MemWrite, not_1_out, in_1[1], not_3_out, in_1[3]);
  not not_5 (RegWrite, MemWrite);
  not not_6 (not_6_out, MemRead);
  not not_7 (not_7_out, and_2_out);
  not not_8 (not_8_out, and_1_out);
  or or_1 (or_1_out, MemRead, MemWrite);
  Multiplexer #(.width(4), .enable("false")) multiplexer_2 (
    .in0(multiplexer_1_out), .in1(4'b0000), .out(ALU), .sel(or_1_out));

  assign MemToReg = MemRead;

  // Notes on the sheet:
  //   Unary
  //   Binary
  //   Lw
  //   Sw
endmodule
